// Logisim project 8255A_0.circ as structural Verilog: 3 circuits, main circuit main
module main (
  input  in_1,
  input  in_2,
  input  in_3,
  input  in_4,
  input  in_5,
  input  in_6,
  input  [7:0] in_7,
  input  in_8,
  input  in_9,
  input  in_10
);

  wire [7:0] a_8255a_0_1_out_10, a_8255a_0_1_out_11, a_8255a_0_1_out_12, register_1_q;

  A_8255A_0 a_8255a_0_1 (
    .in_1(register_1_q), .in_6(in_6), .in_8(in_8), .in_4(in_7), .in_3(in_4), .in_5(in_5), .in_7(in_9),
    .in_9(in_10), .out_10(a_8255a_0_1_out_10), .out_11(a_8255a_0_1_out_11), .out_12(a_8255a_0_1_out_12));  // open: in_2
  Register register_1 (.D(a_8255a_0_1_out_10), .en(in_1), .clk(in_2), .Q(register_1_q), .clr(in_3));
  // Probe on register_1_q
  // Probe on a_8255a_0_1_out_10
  Hex_Digit_Display hex_digit_display_1 (.value(a_8255a_0_1_out_11[7:4]));  // open: dp
  Hex_Digit_Display hex_digit_display_2 (.value(a_8255a_0_1_out_11[3:0]));  // open: dp
endmodule

module A_8255A_0 (
  input  [7:0] in_1,
  input  [7:0] in_2,
  input  in_3,
  input  [7:0] in_4,
  input  in_5,
  input  in_6,
  input  in_7,
  input  in_8,
  input  in_9,
  output [7:0] out_10,
  output [7:0] out_11,
  output [7:0] out_12
);

  wire AConFor, BConFor, decoder_8255a_1_out_8, decoder_8255a_1_out_9, decoder_8255a_1_out_10,
       decoder_8255a_1_out_11, decoder_8255a_1_out_12, decoder_8255a_1_out_13, decoder_8255a_1_out_14,
       decoder_8255a_1_out_15, decoder_8255a_1_out_16, priority_encoder_1_gs;
  wire [1:0] Code;
  wire [7:0] multiplexer_1_out, register_3_q, register_4_q, register_5_q;

  Decoder_8255A decoder_8255a_1 (
    .in_3(in_5), .in_5(in_7), .in_6(in_9), .in_7(in_8), .INPUT(in_3), .in_4(BConFor), .in_2(AConFor),
    .out_10(decoder_8255a_1_out_10), .out_11(decoder_8255a_1_out_11), .out_13(decoder_8255a_1_out_13),
    .out_15(decoder_8255a_1_out_15), .out_8(decoder_8255a_1_out_8), .out_12(decoder_8255a_1_out_12),
    .out_14(decoder_8255a_1_out_14), .out_16(decoder_8255a_1_out_16), .out_9(decoder_8255a_1_out_9));
  Priority_Encoder #(.select(2)) priority_encoder_1 (
    .in0(decoder_8255a_1_out_8), .in1(decoder_8255a_1_out_11), .in2(decoder_8255a_1_out_13),
    .in3(decoder_8255a_1_out_15), .out(Code), .gs(priority_encoder_1_gs), .en_in(1'b1));  // open: en_out
  Register #(.trigger("high")) register_1 (
    .D(in_1), .en(decoder_8255a_1_out_9), .clk(decoder_8255a_1_out_9), .Q(out_11), .clr(in_6));
  Register #(.trigger("high")) register_2 (
    .D(in_1), .en(decoder_8255a_1_out_14), .clk(decoder_8255a_1_out_14), .Q(out_12), .clr(in_6));
  Register #(.trigger("high")) register_3 (
    .D(in_1), .en(decoder_8255a_1_out_10), .clk(decoder_8255a_1_out_10),
    .Q({register_3_q[7:5], AConFor, register_3_q[3:2], BConFor, register_3_q[0]}), .clr(in_6));
  Register #(.trigger("high")) register_4 (
    .D(in_2), .en(decoder_8255a_1_out_12), .clk(decoder_8255a_1_out_12), .Q(register_4_q), .clr(in_6));
  Register #(.trigger("high")) register_5 (
    .D(in_4), .en(decoder_8255a_1_out_16), .clk(decoder_8255a_1_out_16), .Q(register_5_q), .clr(in_6));
  Multiplexer #(.select(2), .width(8)) multiplexer_1 (
    .in0(out_11), .in1(register_4_q), .in2(out_12), .in3(register_5_q), .out(multiplexer_1_out), .sel(Code));
  assign out_10 = priority_encoder_1_gs ? multiplexer_1_out : 8'bz;  // Controlled_Buffer controlled_buffer_1

  // Other names for the same wires on the sheet: A0 = in_7; A1 = in_9; CS = in_8; DATA_IN[7:0] = in_1;
  //   DATA_OUT[7:0] = out_10; PA_IN[7:0] = in_2; PA_OUT[7:0] = out_11; PB_IN[7:0] = in_4; PB_OUT[7:0] = out_12;
  //   RD = in_3; RESET = in_6; WR = in_5

  // Notes on the sheet:
  //   INPUT
  //   OUTPUT
endmodule

module Decoder_8255A (
  input  INPUT,
  input  in_2,
  input  in_3,
  input  in_4,
  input  in_5,
  input  in_6,
  input  in_7,
  output out_8,
  output out_9,
  output out_10,
  output out_11,
  output out_12,
  output out_13,
  output out_14,
  output out_15,
  output out_16
);

  wire decoder_1_out0, decoder_1_out1, decoder_1_out2, decoder_1_out3;

  Decoder #(.select(2)) decoder_1 (
    .out0(decoder_1_out0), .out1(decoder_1_out1), .out2(decoder_1_out2), .out3(decoder_1_out3),
    .sel({in_6, in_5}), .en(in_7));
  and and_1 (out_8, decoder_1_out0, INPUT, ~in_2);  // AND_Gate
  and and_2 (out_11, decoder_1_out0, INPUT, in_2);
  and and_3 (out_9, decoder_1_out0, in_3);
  and and_4 (out_13, decoder_1_out1, INPUT, ~in_4);  // AND_Gate
  and and_5 (out_15, decoder_1_out1, INPUT, in_4);
  and and_6 (out_14, decoder_1_out1, in_3);
  and and_7 (out_10, decoder_1_out3, in_3);
  nand nand_1 (out_12, INPUT, decoder_1_out0);
  nand nand_2 (out_16, INPUT, decoder_1_out1);

  // Other names for the same wires on the sheet: A0 = in_5; A1 = in_6; A_0_R = out_8; A_0_W = out_9; A_1_R = out_11;
  //   A_1_W = out_12; AContorlFormat = in_2; B_0_R = out_13; B_0_W = out_14; B_1_R = out_15; B_1_W = out_16;
  //   BContorlFormat = in_4; CS = in_7; PSW_0_W = out_10; RD = INPUT; WR = in_3

  // Notes on the sheet:
  //   OUTPUT
endmodule
